# Fritzing sketch gpio-grove-pir-and-led (saved by Fritzing 0.9.2b)

parts:
  パーツ1 = CHIRIMEN
  Grove_LED1 = Grove Chainable RGB LED
  Grove_LED2 = Grove Chainable RGB LED
  Grove_LED3 = Grove Chainable RGB LED
  Grove_PIR_Motion_Sensor = Grove Rotary Angle Sensor

nets:
  N1: パーツ1.CN2-1_GND, Grove_LED1.VCC#1
  N2: パーツ1.CN2-4_GND, Grove_LED1.CI
  N3: パーツ1.CN2-5_ALOUT, パーツ1.CN1-9_SPI0_RX, Grove_LED1.DI
  N4: パーツ1.CN1-1_GND, Grove_PIR_Motion_Sensor.VCC
  N5: パーツ1.CN1-7_SPI0_CS, Grove_PIR_Motion_Sensor.NC
  N6: パーツ1.CN1-10_SPI0_TX, Grove_PIR_Motion_Sensor.SIG
  N7: パーツ1.CN1-18_VCC_5V, Grove_PIR_Motion_Sensor.GND
  N8: パーツ1.CN2-18_VSYS(5V), Grove_LED1.GND#0
  N9: Grove_LED1.GND#4, Grove_LED2.GND#0
  N10: Grove_LED1.VCC#5, Grove_LED2.VCC#1
  N11: Grove_LED1.DO, Grove_LED2.DI
  N12: Grove_LED1.CO, Grove_LED2.CI
  N13: Grove_LED2.GND#4, Grove_LED3.GND
  N14: Grove_LED2.VCC#5, Grove_LED3.VCC
  N15: Grove_LED2.DO, Grove_LED3.DI
  N16: Grove_LED2.CO, Grove_LED3.CI
  N17: Grove_LED3.DO, Grove_LED3.CO

custom parts:
  CHIRIMEN: CHIRIMEN board.
  Grove Chainable RGB LED: A chainable RGB LED
  Grove Rotary Angle Sensor: A potentiometer
